// Logisim project total16.circ as structural Verilog: 4 circuits, main circuit main
module main (
);

  wire buffer_2_out, comparator_1_eq, comparator_1_gt, comparator_1_lt, HILO_WR, not_1_out, not_2_out,
       OP_ALU, OP_OTHER, RAM_RW, sys_clk, sys_rst, undriven;
  wire [4:0] alu_1_output_0_addr, alu_1_output_1_addr, alu_1_read_0_addr, alu_1_read_1_addr,
       memio_1_register_1_read_address, memio_1_register_read_address, memio_1_register_write_address,
       READ_0_ADDR, READ_1_ADDR, WRITE_0_ADDR, WRITE_1_ADDR;
  wire [5:0] ALU_OPCODE, memio_1_opcode_out, OPCODE, OTHER_OPCODE;
  wire [9:0] ALU_DATA, INSTR_DATA, memio_1_instr_data_in_2, OTHER_DATA;
  wire [15:0] alu_1_output_0, alu_1_output_1, buffer_3_out, CMP_DIR_OUT, controlled_buffer_7_out,
       controlled_buffer_8_out, controlled_buffer_9_out, controlled_buffer_18_out, dataBus_0, dataBus_1,
       HI_IN, LO_IN, memio_1_register_x_to_write, pc, ram_1_data, ram_access_addr, RAMDATA_IN, RAMDATA_OUT,
       registers_1_gpr0_out, sp, WRITE_0_DATA, WRITE_1_DATA;

  Clock clock_1 (.out(sys_clk));
  Button Reset (.out(sys_rst));
  Pull_Resistor pull_resistor_1 (.node(ram_access_addr));
  assign ALU_OPCODE = OP_ALU ? OPCODE : 6'bz;  // Controlled_Buffer controlled_buffer_1
  assign OTHER_OPCODE = OP_OTHER ? OPCODE : 6'bz;  // Controlled_Buffer controlled_buffer_2
  assign ALU_DATA = OP_ALU ? INSTR_DATA : 10'bz;  // Controlled_Buffer controlled_buffer_3
  assign OTHER_DATA = OP_OTHER ? INSTR_DATA : 10'bz;  // Controlled_Buffer controlled_buffer_4
  ROM #(.addrWidth(16), .dataWidth(16)) rom_1 (.addr(pc), .data({OPCODE, INSTR_DATA}), .sel(1'b1));
  Pull_Resistor pull_resistor_2 (.node(OTHER_OPCODE));
  Pull_Resistor pull_resistor_3 (.node(OTHER_DATA));
  RAM #(.addrWidth(16), .dataWidth(16)) ram_1 (
    .addr(ram_access_addr), .data(ram_1_data), .sel(1'b1), .clk(sys_clk), .ld(not_2_out), .clr(undriven));
  Comparator #(.width(6), .mode("unsigned")) comparator_1 (
    .a(OPCODE), .b(6'b011010), .gt(comparator_1_gt), .eq(comparator_1_eq), .lt(comparator_1_lt));
  buf buffer_1 (OP_ALU, comparator_1_lt);
  assign RAMDATA_OUT = not_1_out ? ram_1_data : 16'bz;  // Controlled_Buffer controlled_buffer_5
  not not_1 (not_1_out, RAM_RW);
  assign ram_1_data = buffer_2_out ? RAMDATA_IN : 16'bz;  // Controlled_Buffer controlled_buffer_6
  not not_2 (not_2_out, RAM_RW);
  or or_1 (OP_OTHER, comparator_1_gt, comparator_1_eq);
  buf buffer_2 (buffer_2_out, RAM_RW);
  assign controlled_buffer_7_out = OP_ALU ? dataBus_0 : 16'bz;  // Controlled_Buffer controlled_buffer_7
  assign controlled_buffer_8_out = OP_ALU ? dataBus_1 : 16'bz;  // Controlled_Buffer controlled_buffer_8
  assign buffer_3_out = controlled_buffer_7_out;  // Buffer buffer_3, 16 bits wide
  ALU alu_1 (
    .DATA(ALU_DATA), .OPCODE(ALU_OPCODE), .OUTPUT_0(alu_1_output_0), .INPUT_0(buffer_3_out),
    .INPUT_1(controlled_buffer_8_out), .OUTPUT_1(alu_1_output_1), .OUTPUT_0_ADDR(alu_1_output_0_addr),
    .OUTPUT_1_ADDR(alu_1_output_1_addr), .READ_0_ADDR(alu_1_read_0_addr), .READ_1_ADDR(alu_1_read_1_addr),
    .HI_OUT(HI_IN), .LO_OUT(LO_IN), .HILO_DIR_WR(HILO_WR));  // open: CARRY_OUT
  MEMIO memio_1 (
    .OPCODE_IN(OTHER_OPCODE), .INSTR_DATA_IN(OTHER_DATA), .OPCODE_OUT(memio_1_opcode_out),
    .INSTR_DATA_IN_2(memio_1_instr_data_in_2), .SYS_CLK_IN(sys_clk), .RAM_R_W(RAM_RW),
    .RAM_ADDR(ram_access_addr), .RAM_DATA_IN(RAMDATA_OUT), .RAM_DATA_OUT(RAMDATA_IN),
    .REGISTER_X_READ(controlled_buffer_18_out), .REGISTER_X_TO_WRITE(memio_1_register_x_to_write),
    .REGISTER_READ_ADDRESS(memio_1_register_read_address),
    .REGISTER_WRITE_ADDRESS(memio_1_register_write_address),
    .REGISTER_1_READ_ADDRESS(memio_1_register_1_read_address), .REGISTER_1_X_READ(controlled_buffer_9_out));
  assign controlled_buffer_9_out = OP_OTHER ? dataBus_1 : 16'bz;  // Controlled_Buffer controlled_buffer_9
  assign READ_1_ADDR = OP_ALU ? alu_1_read_1_addr : 5'bz;  // Controlled_Buffer controlled_buffer_10
  assign WRITE_0_ADDR = OP_ALU ? alu_1_output_0_addr : 5'bz;  // Controlled_Buffer controlled_buffer_11
  assign WRITE_0_DATA = OP_ALU ? alu_1_output_0 : 16'bz;  // Controlled_Buffer controlled_buffer_12
  assign WRITE_0_ADDR = OP_OTHER ? memio_1_register_write_address : 5'bz;  // Controlled_Buffer controlled_buffer_13
  assign READ_1_ADDR = OP_OTHER ? memio_1_register_1_read_address : 5'bz;  // Controlled_Buffer controlled_buffer_14
  REGISTERS registers_1 (
    .clk_in(sys_clk), .SYS_RESET(sys_rst), .HI_IN(HI_IN), .LO_IN(LO_IN), .READ_1(READ_1_ADDR),
    .READ_0(READ_0_ADDR), .WRITE_0(WRITE_0_ADDR), .WRITE_1(WRITE_1_ADDR), .DATA_IN_0(WRITE_0_DATA),
    .DATA_IN_1(WRITE_1_DATA), .OUTPUT_0(dataBus_0), .SP_OUT(sp), .GPR0_OUT(registers_1_gpr0_out),
    .OUTPUT_1(dataBus_1), .PC_OUT(pc), .HI_LO_WR(HILO_WR), .CMP_DIR_OUT(CMP_DIR_OUT));  // open: CARRY_DIR_WR, CMP_DIR_IN, CMP_DIR_WR, CARRY_DIR_OUT, CARRY_DIR_IN
  assign READ_0_ADDR = OP_ALU ? alu_1_read_0_addr : 5'bz;  // Controlled_Buffer controlled_buffer_15
  assign WRITE_1_ADDR = OP_ALU ? alu_1_output_1_addr : 5'bz;  // Controlled_Buffer controlled_buffer_16
  assign WRITE_1_DATA = OP_ALU ? alu_1_output_1 : 16'bz;  // Controlled_Buffer controlled_buffer_17
  assign controlled_buffer_18_out = OP_OTHER ? dataBus_0 : 16'bz;  // Controlled_Buffer controlled_buffer_18
  assign WRITE_0_DATA = OP_OTHER ? memio_1_register_x_to_write : 16'bz;  // Controlled_Buffer controlled_buffer_19
  assign READ_0_ADDR = OP_OTHER ? memio_1_register_read_address : 5'bz;  // Controlled_Buffer controlled_buffer_20

  // Notes on the sheet:
  //   16 bit PROG MEM
  //   If OPCODE < 0x1A it is an ALU Call, otherwise something else
  //   contents of rom_1 (hex, n*v repeats v):
  //   0 c41 6c22 0 0 37ff 4422 6800 0 6c20
  //   Registers
endmodule

module ALU (
  input  [15:0] INPUT_0,
  input  [15:0] INPUT_1,
  input  [9:0] DATA,
  input  [5:0] OPCODE,
  output [15:0] HI_OUT,
  output [15:0] OUTPUT_0,
  output [15:0] OUTPUT_1,
  output [15:0] LO_OUT,
  output [4:0] OUTPUT_0_ADDR,
  output [15:0] CARRY_OUT,
  output [4:0] OUTPUT_1_ADDR,
  output HILO_DIR_WR,
  output [4:0] READ_0_ADDR,
  output [4:0] READ_1_ADDR
);

  wire ADD, ADDI, AND, ANDI, buffer_1_out, buffer_2_out, buffer_3_out, buffer_4_out, buffer_6_out,
       buffer_7_out, buffer_8_out, buffer_9_out, buffer_10_out, buffer_11_out, buffer_12_out, buffer_13_out,
       buffer_24_out, buffer_25_out, buffer_26_out, buffer_27_out, carry_out_t, controlled_buffer_42_out,
       controlled_buffer_44_out, controlled_buffer_46_out, controlled_buffer_48_out,
       controlled_buffer_50_out, controlled_buffer_52_out, controlled_buffer_54_out,
       controlled_buffer_56_out, controlled_buffer_58_out, controlled_buffer_60_out, DIV, IMM_EN, LI, LMUL,
       LOI, LSI, LSL, MOV, MUL, NOP, NOT, not_2_out, not_3_out, not_4_out, not_5_out, not_6_out, not_7_out,
       not_8_out, not_9_out, not_10_out, not_11_out, not_12_out, not_13_out, not_14_out, not_15_out,
       not_16_out, OR, or_1_out, or_2_out, or_3_out, or_4_out, or_6_out, or_7_out, or_8_out, or_9_out,
       or_11_out, or_12_out, or_13_out, or_14_out, or_18_out, or_19_out, or_20_out, or_21_out, ORI, ROTL,
       RSA, RSI, RSL, SUB, SUBI, SWP, UADD, USUB, XOR;
  wire [4:0] immediate_content;
  wire [9:0] pull_resistor_24_node;
  wire [15:0] adder_1_out, AND_out, arg1, arg2, bit_extender_1_out, bit_extender_3_out, buffer_17_out,
       buffer_18_out, buffer_20_out, buffer_21_out, buffer_22_out, buffer_23_out, controlled_buffer_25_out,
       controlled_buffer_26_out, controlled_buffer_27_out, controlled_buffer_28_out,
       controlled_buffer_29_out, controlled_buffer_30_out, controlled_buffer_31_out,
       controlled_buffer_32_out, controlled_buffer_33_out, controlled_buffer_34_out,
       controlled_buffer_35_out, controlled_buffer_36_out, controlled_buffer_37_out,
       controlled_buffer_38_out, controlled_buffer_39_out, controlled_buffer_40_out, divider_1_out, hiwr_0,
       hiwr_1, lowr_0, multiplier_1_out, not_1_out, OR_5_out, OUTPUT_DATA_1, pull_resistor_2_node,
       pull_resistor_3_node, pull_resistor_4_node, pull_resistor_5_node, pull_resistor_6_node,
       pull_resistor_7_node, pull_resistor_8_node, pull_resistor_9_node, pull_resistor_10_node,
       pull_resistor_11_node, pull_resistor_12_node, pull_resistor_13_node, pull_resistor_14_node,
       pull_resistor_15_node, pull_resistor_16_node, pull_resistor_17_node, shifter_1_out, shifter_2_out,
       shifter_3_out, shifter_4_out, subtractor_1_out, subtractor_2_out, xor_1_out;

  or or_1 (or_1_out, ORI, OR);
  or or_2 (or_2_out, ANDI, AND);
  buf buffer_1 (buffer_1_out, XOR);
  buf buffer_2 (buffer_2_out, NOT);
  or or_3 (or_3_out, LSL, LSI);
  or or_4 (or_4_out, RSL, RSI);
  buf buffer_3 (buffer_3_out, RSA);
  buf buffer_4 (buffer_4_out, ROTL);
  Pull_Resistor pull_resistor_1 (.node(OPCODE));
  Demultiplexer #(.select(5)) demultiplexer_1 (
    .out0(NOP), .out1(MOV), .out2(SWP), .out3(LI), .out4(ADD), .out5(UADD), .out6(SUB), .out7(USUB),
    .out8(ADDI), .out9(SUBI), .out10(MUL), .out11(LMUL), .out12(DIV), .out13(LOI), .out14(LSL), .out15(LSI),
    .out16(RSL), .out17(RSI), .out18(RSA), .out19(ROTL), .out20(AND), .out21(OR), .out22(XOR), .out23(NOT),
    .out24(ANDI), .out25(ORI), .in(1'b1), .sel(OPCODE[4:0]), .en(1'b1));  // open: out26, out27, out28, out29, out30, out31
  Pull_Resistor pull_resistor_2 (.node(pull_resistor_2_node));
  assign pull_resistor_2_node = or_1_out ? arg1 : 16'bz;  // Controlled_Buffer controlled_buffer_1
  Pull_Resistor pull_resistor_3 (.node(pull_resistor_3_node));
  assign pull_resistor_3_node = or_1_out ? arg2 : 16'bz;  // Controlled_Buffer controlled_buffer_2
  Pull_Resistor pull_resistor_4 (.node(pull_resistor_4_node));
  assign pull_resistor_4_node = or_2_out ? arg1 : 16'bz;  // Controlled_Buffer controlled_buffer_3
  Pull_Resistor pull_resistor_5 (.node(pull_resistor_5_node));
  assign pull_resistor_5_node = or_2_out ? arg2 : 16'bz;  // Controlled_Buffer controlled_buffer_4
  Pull_Resistor pull_resistor_6 (.node(pull_resistor_6_node));
  assign pull_resistor_6_node = buffer_1_out ? arg1 : 16'bz;  // Controlled_Buffer controlled_buffer_5
  Pull_Resistor pull_resistor_7 (.node(pull_resistor_7_node));
  assign pull_resistor_7_node = buffer_1_out ? arg2 : 16'bz;  // Controlled_Buffer controlled_buffer_6
  Pull_Resistor pull_resistor_8 (.node(pull_resistor_8_node));
  assign pull_resistor_8_node = buffer_2_out ? arg1 : 16'bz;  // Controlled_Buffer controlled_buffer_7
  Pull_Resistor pull_resistor_9 (.node(pull_resistor_9_node));
  assign pull_resistor_9_node = buffer_2_out ? arg2 : 16'bz;  // Controlled_Buffer controlled_buffer_8
  Pull_Resistor pull_resistor_10 (.node(pull_resistor_10_node));
  assign pull_resistor_10_node = or_3_out ? arg1 : 16'bz;  // Controlled_Buffer controlled_buffer_9
  Pull_Resistor pull_resistor_11 (.node(pull_resistor_11_node));
  assign pull_resistor_11_node = or_3_out ? arg2 : 16'bz;  // Controlled_Buffer controlled_buffer_10
  Pull_Resistor pull_resistor_12 (.node(pull_resistor_12_node));
  assign pull_resistor_12_node = or_4_out ? arg1 : 16'bz;  // Controlled_Buffer controlled_buffer_11
  Pull_Resistor pull_resistor_13 (.node(pull_resistor_13_node));
  assign pull_resistor_13_node = or_4_out ? arg2 : 16'bz;  // Controlled_Buffer controlled_buffer_12
  Pull_Resistor pull_resistor_14 (.node(pull_resistor_14_node));
  assign pull_resistor_14_node = buffer_3_out ? arg1 : 16'bz;  // Controlled_Buffer controlled_buffer_13
  Pull_Resistor pull_resistor_15 (.node(pull_resistor_15_node));
  assign pull_resistor_15_node = buffer_3_out ? arg2 : 16'bz;  // Controlled_Buffer controlled_buffer_14
  Pull_Resistor pull_resistor_16 (.node(pull_resistor_16_node));
  assign pull_resistor_16_node = buffer_4_out ? arg1 : 16'bz;  // Controlled_Buffer controlled_buffer_15
  Pull_Resistor pull_resistor_17 (.node(pull_resistor_17_node));
  assign pull_resistor_17_node = buffer_4_out ? arg2 : 16'bz;  // Controlled_Buffer controlled_buffer_16
  assign bit_extender_1_out = {{11{1'b0}}, immediate_content};  // Bit_Extender bit_extender_1
  assign OR_5_out = pull_resistor_2_node | pull_resistor_3_node;  // OR_Gate OR_5, 16 bits wide
  assign AND_out = pull_resistor_4_node & pull_resistor_5_node;  // AND_Gate AND, 16 bits wide
  Shifter #(.width(16)) shifter_1 (
    .in(pull_resistor_10_node), .\dist (pull_resistor_11_node[3:0]), .out(shifter_1_out));
  Shifter #(.width(16), .shift("lr")) shifter_2 (
    .in(pull_resistor_12_node), .\dist (pull_resistor_13_node[3:0]), .out(shifter_2_out));
  Shifter #(.width(16), .shift("ar")) shifter_3 (
    .in(pull_resistor_14_node), .\dist (pull_resistor_15_node[3:0]), .out(shifter_3_out));
  Shifter #(.width(16), .shift("rl")) shifter_4 (
    .in(pull_resistor_16_node), .\dist (pull_resistor_17_node[3:0]), .out(shifter_4_out));
  assign arg1 = INPUT_0;  // Buffer buffer_5, 16 bits wide
  Multiplexer #(.width(16)) multiplexer_1 (
    .in0(INPUT_1), .in1(bit_extender_1_out), .out(arg2), .sel(IMM_EN), .en(1'b1));
  or or_6 (or_6_out, ORI, OR);
  assign hiwr_0 = or_6_out ? OR_5_out : 16'bz;  // Controlled_Buffer controlled_buffer_17
  or or_7 (or_7_out, ANDI, AND);
  assign hiwr_0 = or_7_out ? AND_out : 16'bz;  // Controlled_Buffer controlled_buffer_18
  buf buffer_6 (buffer_6_out, XOR);
  assign hiwr_0 = buffer_6_out ? xor_1_out : 16'bz;  // Controlled_Buffer controlled_buffer_19
  assign xor_1_out = pull_resistor_6_node ^ pull_resistor_7_node;  // XOR_Gate xor_1, 16 bits wide
  buf buffer_7 (buffer_7_out, NOT);
  assign hiwr_0 = buffer_7_out ? not_1_out : 16'bz;  // Controlled_Buffer controlled_buffer_20
  assign not_1_out = ~pull_resistor_8_node;  // NOT_Gate not_1, 16 bits wide
  or or_8 (or_8_out, LSL, LSI);
  assign hiwr_0 = or_8_out ? shifter_1_out : 16'bz;  // Controlled_Buffer controlled_buffer_21
  or or_9 (or_9_out, RSL, RSI);
  assign hiwr_0 = or_9_out ? shifter_2_out : 16'bz;  // Controlled_Buffer controlled_buffer_22
  buf buffer_8 (buffer_8_out, RSA);
  assign hiwr_0 = buffer_8_out ? shifter_3_out : 16'bz;  // Controlled_Buffer controlled_buffer_23
  buf buffer_9 (buffer_9_out, ROTL);
  assign hiwr_0 = buffer_9_out ? shifter_4_out : 16'bz;  // Controlled_Buffer controlled_buffer_24
  Pull_Resistor pull_resistor_18 (.node(HI_OUT));
  Pull_Resistor pull_resistor_19 (.node(LO_OUT));
  assign CARRY_OUT = {{15{1'b0}}, carry_out_t};  // Bit_Extender bit_extender_2
  Pull_Resistor pull_resistor_20 (.node(CARRY_OUT));
  Pull_Resistor pull_resistor_21 (.node(HILO_DIR_WR));
  or or_10 (IMM_EN, ANDI, RSI, LSI, SUBI, ADDI, LI);
  Pull_Resistor pull_resistor_22 (.node(hiwr_0));
  Pull_Resistor pull_resistor_23 (.node(OUTPUT_DATA_1));
  or or_11 (or_11_out, ADDI, ADD);
  or or_12 (or_12_out, SUBI, SUB);
  or or_13 (or_13_out, SUBI, SUB);
  or or_14 (or_14_out, MUL, LMUL);
  buf buffer_10 (buffer_10_out, DIV);
  buf buffer_11 (buffer_11_out, LI);
  buf buffer_12 (buffer_12_out, SWP);
  buf buffer_13 (buffer_13_out, MOV);
  Pull_Resistor pull_resistor_24 (.node(pull_resistor_24_node));
  assign OUTPUT_1_ADDR = READ_1_ADDR;  // Buffer buffer_14, 5 bits wide
  assign OUTPUT_0_ADDR = READ_0_ADDR;  // Buffer buffer_15, 5 bits wide
  assign OUTPUT_0 = buffer_17_out;  // Buffer buffer_16, 16 bits wide
  assign buffer_17_out = hiwr_0;  // Buffer buffer_17, 16 bits wide
  assign buffer_18_out = OUTPUT_DATA_1;  // Buffer buffer_18, 16 bits wide
  assign OUTPUT_1 = buffer_18_out;  // Buffer buffer_19, 16 bits wide
  assign controlled_buffer_25_out = or_11_out ? arg1 : 16'bz;  // Controlled_Buffer controlled_buffer_25
  assign controlled_buffer_26_out = or_11_out ? arg2 : 16'bz;  // Controlled_Buffer controlled_buffer_26
  assign controlled_buffer_27_out = or_12_out ? arg1 : 16'bz;  // Controlled_Buffer controlled_buffer_27
  assign controlled_buffer_28_out = or_12_out ? arg2 : 16'bz;  // Controlled_Buffer controlled_buffer_28
  assign controlled_buffer_29_out = or_13_out ? arg1 : 16'bz;  // Controlled_Buffer controlled_buffer_29
  assign controlled_buffer_30_out = or_13_out ? arg2 : 16'bz;  // Controlled_Buffer controlled_buffer_30
  assign controlled_buffer_31_out = or_14_out ? arg1 : 16'bz;  // Controlled_Buffer controlled_buffer_31
  assign controlled_buffer_32_out = or_14_out ? arg2 : 16'bz;  // Controlled_Buffer controlled_buffer_32
  assign controlled_buffer_33_out = buffer_10_out ? arg1 : 16'bz;  // Controlled_Buffer controlled_buffer_33
  assign controlled_buffer_34_out = buffer_10_out ? arg2 : 16'bz;  // Controlled_Buffer controlled_buffer_34
  assign controlled_buffer_35_out = buffer_11_out ? arg1 : 16'bz;  // Controlled_Buffer controlled_buffer_35
  assign controlled_buffer_36_out = buffer_11_out ? arg2 : 16'bz;  // Controlled_Buffer controlled_buffer_36
  assign controlled_buffer_37_out = buffer_12_out ? arg1 : 16'bz;  // Controlled_Buffer controlled_buffer_37
  assign controlled_buffer_38_out = buffer_12_out ? arg2 : 16'bz;  // Controlled_Buffer controlled_buffer_38
  assign controlled_buffer_39_out = buffer_13_out ? arg1 : 16'bz;  // Controlled_Buffer controlled_buffer_39
  assign controlled_buffer_40_out = buffer_13_out ? arg2 : 16'bz;  // Controlled_Buffer controlled_buffer_40
  Pull_Resistor pull_resistor_25 (.node(OUTPUT_0));
  Pull_Resistor pull_resistor_26 (.node(OUTPUT_1));
  Pull_Resistor pull_resistor_27 (.node(OUTPUT_0_ADDR));
  Pull_Resistor pull_resistor_28 (.node(OUTPUT_1_ADDR));
  Pull_Resistor pull_resistor_29 (.node(READ_0_ADDR));
  Pull_Resistor pull_resistor_30 (.node(READ_1_ADDR));
  assign pull_resistor_24_node[0] = LOI ? DATA[0] : 1'bz;  // Controlled_Buffer controlled_buffer_41
  assign controlled_buffer_42_out = not_2_out ? DATA[0] : 1'bz;  // Controlled_Buffer controlled_buffer_42
  not not_2 (not_2_out, LOI);
  assign pull_resistor_24_node[1] = LOI ? DATA[1] : 1'bz;  // Controlled_Buffer controlled_buffer_43
  assign controlled_buffer_44_out = not_3_out ? DATA[1] : 1'bz;  // Controlled_Buffer controlled_buffer_44
  not not_3 (not_3_out, LOI);
  assign pull_resistor_24_node[2] = LOI ? DATA[2] : 1'bz;  // Controlled_Buffer controlled_buffer_45
  assign controlled_buffer_46_out = not_4_out ? DATA[2] : 1'bz;  // Controlled_Buffer controlled_buffer_46
  not not_4 (not_4_out, LOI);
  assign pull_resistor_24_node[3] = LOI ? DATA[3] : 1'bz;  // Controlled_Buffer controlled_buffer_47
  assign controlled_buffer_48_out = not_5_out ? DATA[3] : 1'bz;  // Controlled_Buffer controlled_buffer_48
  not not_5 (not_5_out, LOI);
  assign pull_resistor_24_node[4] = LOI ? DATA[4] : 1'bz;  // Controlled_Buffer controlled_buffer_49
  assign controlled_buffer_50_out = not_6_out ? DATA[4] : 1'bz;  // Controlled_Buffer controlled_buffer_50
  not not_6 (not_6_out, LOI);
  assign pull_resistor_24_node[5] = LOI ? DATA[5] : 1'bz;  // Controlled_Buffer controlled_buffer_51
  assign controlled_buffer_52_out = not_7_out ? DATA[5] : 1'bz;  // Controlled_Buffer controlled_buffer_52
  not not_7 (not_7_out, LOI);
  assign pull_resistor_24_node[6] = LOI ? DATA[6] : 1'bz;  // Controlled_Buffer controlled_buffer_53
  assign controlled_buffer_54_out = not_8_out ? DATA[6] : 1'bz;  // Controlled_Buffer controlled_buffer_54
  not not_8 (not_8_out, LOI);
  assign pull_resistor_24_node[7] = LOI ? DATA[7] : 1'bz;  // Controlled_Buffer controlled_buffer_55
  assign controlled_buffer_56_out = not_9_out ? DATA[7] : 1'bz;  // Controlled_Buffer controlled_buffer_56
  not not_9 (not_9_out, LOI);
  assign pull_resistor_24_node[8] = LOI ? DATA[8] : 1'bz;  // Controlled_Buffer controlled_buffer_57
  assign controlled_buffer_58_out = not_10_out ? DATA[8] : 1'bz;  // Controlled_Buffer controlled_buffer_58
  not not_10 (not_10_out, LOI);
  assign pull_resistor_24_node[9] = LOI ? DATA[9] : 1'bz;  // Controlled_Buffer controlled_buffer_59
  assign controlled_buffer_60_out = not_11_out ? DATA[9] : 1'bz;  // Controlled_Buffer controlled_buffer_60
  not not_11 (not_11_out, LOI);
  Pull_Resistor pull_resistor_31 (.node(controlled_buffer_25_out));
  Pull_Resistor pull_resistor_32 (.node(controlled_buffer_26_out));
  Pull_Resistor pull_resistor_33 (.node(controlled_buffer_27_out));
  Pull_Resistor pull_resistor_34 (.node(controlled_buffer_28_out));
  Pull_Resistor pull_resistor_35 (.node(controlled_buffer_29_out));
  Pull_Resistor pull_resistor_36 (.node(controlled_buffer_30_out));
  Pull_Resistor pull_resistor_37 (.node(controlled_buffer_31_out));
  Pull_Resistor pull_resistor_38 (.node(controlled_buffer_32_out));
  Pull_Resistor pull_resistor_39 (.node(controlled_buffer_33_out));
  Pull_Resistor pull_resistor_40 (.node(controlled_buffer_34_out));
  assign LO_OUT = lowr_0 | hiwr_0;  // OR_Gate or_15, 16 bits wide
  assign HI_OUT = hiwr_0 | hiwr_1;  // OR_Gate or_16, 16 bits wide
  or or_17 (HILO_DIR_WR, DIV, LMUL, MUL);
  Pull_Resistor pull_resistor_41 (.node(controlled_buffer_35_out));
  Pull_Resistor pull_resistor_42 (.node(controlled_buffer_36_out));
  Pull_Resistor pull_resistor_43 (.node(controlled_buffer_37_out));
  Pull_Resistor pull_resistor_44 (.node(controlled_buffer_38_out));
  Pull_Resistor pull_resistor_45 (.node(controlled_buffer_39_out));
  Pull_Resistor pull_resistor_46 (.node(controlled_buffer_40_out));
  assign bit_extender_3_out = {{6{1'b0}}, pull_resistor_24_node};  // Bit_Extender bit_extender_3
  assign hiwr_0 = LOI ? bit_extender_3_out : 16'bz;  // Controlled_Buffer controlled_buffer_61
  assign READ_0_ADDR = LOI ? 5'b00001 : 5'bz;  // Controlled_Buffer controlled_buffer_62
  Adder #(.width(16)) adder_1 (
    .a(controlled_buffer_25_out), .b(controlled_buffer_26_out), .out(adder_1_out), .cout(carry_out_t));  // open: cin
  Subtractor #(.width(16)) subtractor_1 (
    .a(controlled_buffer_27_out), .b(controlled_buffer_28_out), .out(subtractor_1_out), .bout(carry_out_t));  // open: bin
  Subtractor #(.width(16)) subtractor_2 (
    .a(controlled_buffer_29_out), .b(controlled_buffer_30_out), .out(subtractor_2_out), .bout(carry_out_t));  // open: bin
  Multiplier #(.width(16)) multiplier_1 (
    .a(controlled_buffer_31_out), .b(controlled_buffer_32_out), .out(multiplier_1_out), .cout(hiwr_1));  // open: cin
  Divider #(.width(16)) divider_1 (
    .a(controlled_buffer_33_out), .b(controlled_buffer_34_out), .out(divider_1_out), .rem(lowr_0));  // open: upper
  assign buffer_20_out = controlled_buffer_36_out;  // Buffer buffer_20, 16 bits wide
  assign buffer_21_out = controlled_buffer_37_out;  // Buffer buffer_21, 16 bits wide
  assign buffer_22_out = controlled_buffer_38_out;  // Buffer buffer_22, 16 bits wide
  assign buffer_23_out = controlled_buffer_40_out;  // Buffer buffer_23, 16 bits wide
  or or_18 (or_18_out, ADDI, ADD);
  assign hiwr_0 = or_18_out ? adder_1_out : 16'bz;  // Controlled_Buffer controlled_buffer_63
  or or_19 (or_19_out, SUBI, SUB);
  assign hiwr_0 = or_19_out ? subtractor_1_out : 16'bz;  // Controlled_Buffer controlled_buffer_64
  or or_20 (or_20_out, SUBI, SUB);
  assign hiwr_0 = or_20_out ? subtractor_2_out : 16'bz;  // Controlled_Buffer controlled_buffer_65
  or or_21 (or_21_out, LMUL, MUL);
  assign hiwr_0 = or_21_out ? multiplier_1_out : 16'bz;  // Controlled_Buffer controlled_buffer_66
  buf buffer_24 (buffer_24_out, DIV);
  assign hiwr_0 = buffer_24_out ? divider_1_out : 16'bz;  // Controlled_Buffer controlled_buffer_67
  buf buffer_25 (buffer_25_out, LI);
  assign hiwr_0 = buffer_25_out ? buffer_20_out : 16'bz;  // Controlled_Buffer controlled_buffer_68
  buf buffer_26 (buffer_26_out, SWP);
  assign OUTPUT_DATA_1 = buffer_26_out ? buffer_21_out : 16'bz;  // Controlled_Buffer controlled_buffer_69
  assign hiwr_0 = buffer_26_out ? buffer_22_out : 16'bz;  // Controlled_Buffer controlled_buffer_70
  buf buffer_27 (buffer_27_out, MOV);
  assign hiwr_0 = buffer_27_out ? buffer_23_out : 16'bz;  // Controlled_Buffer controlled_buffer_71
  assign immediate_content[0] = IMM_EN ? controlled_buffer_42_out : 1'bz;  // Controlled_Buffer controlled_buffer_72
  assign READ_1_ADDR[0] = not_12_out ? controlled_buffer_42_out : 1'bz;  // Controlled_Buffer controlled_buffer_73
  not not_12 (not_12_out, IMM_EN);
  assign immediate_content[1] = IMM_EN ? controlled_buffer_44_out : 1'bz;  // Controlled_Buffer controlled_buffer_74
  assign READ_1_ADDR[1] = not_13_out ? controlled_buffer_44_out : 1'bz;  // Controlled_Buffer controlled_buffer_75
  not not_13 (not_13_out, IMM_EN);
  assign immediate_content[2] = IMM_EN ? controlled_buffer_46_out : 1'bz;  // Controlled_Buffer controlled_buffer_76
  assign READ_1_ADDR[2] = not_14_out ? controlled_buffer_46_out : 1'bz;  // Controlled_Buffer controlled_buffer_77
  not not_14 (not_14_out, IMM_EN);
  assign immediate_content[3] = IMM_EN ? controlled_buffer_48_out : 1'bz;  // Controlled_Buffer controlled_buffer_78
  assign READ_1_ADDR[3] = not_15_out ? controlled_buffer_48_out : 1'bz;  // Controlled_Buffer controlled_buffer_79
  not not_15 (not_15_out, IMM_EN);
  assign immediate_content[4] = IMM_EN ? controlled_buffer_50_out : 1'bz;  // Controlled_Buffer controlled_buffer_80
  assign READ_1_ADDR[4] = not_16_out ? controlled_buffer_50_out : 1'bz;  // Controlled_Buffer controlled_buffer_81
  not not_16 (not_16_out, IMM_EN);
  buf buffer_28 (READ_0_ADDR[0], controlled_buffer_52_out);
  buf buffer_29 (READ_0_ADDR[1], controlled_buffer_54_out);
  buf buffer_30 (READ_0_ADDR[2], controlled_buffer_56_out);
  buf buffer_31 (READ_0_ADDR[3], controlled_buffer_58_out);
  buf buffer_32 (READ_0_ADDR[4], controlled_buffer_60_out);
  Pull_Resistor pull_resistor_47 (.node(immediate_content));
  Pull_Resistor pull_resistor_48 (.node(READ_1_ADDR));
  Pull_Resistor pull_resistor_49 (.node(READ_0_ADDR));
  // also tied to GND on the sheet: {pull_resistor_9_node[0], pull_resistor_9_node[1], pull_resistor_9_node[2], pull_resistor_9_node[3], pull_resistor_9_node[4], pull_resistor_9_node[5], pull_resistor_9_node[6], pull_resistor_9_node[7], pull_resistor_9_node[8], pull_resistor_9_node[9], pull_resistor_9_node[10], pull_resistor_9_node[11], pull_resistor_9_node[12], pull_resistor_9_node[13], pull_resistor_9_node[14], pull_resistor_9_node[15], pull_resistor_11_node[4], pull_resistor_11_node[5], pull_resistor_11_node[6], pull_resistor_11_node[7], pull_resistor_11_node[8], pull_resistor_11_node[9], pull_resistor_11_node[10], pull_resistor_11_node[11], pull_resistor_11_node[12], pull_resistor_11_node[13], pull_resistor_11_node[14], pull_resistor_11_node[15], pull_resistor_13_node[4], pull_resistor_13_node[5], pull_resistor_13_node[6], pull_resistor_13_node[7], pull_resistor_13_node[8], pull_resistor_13_node[9], pull_resistor_13_node[10], pull_resistor_13_node[11], pull_resistor_13_node[12], pull_resistor_13_node[13], pull_resistor_13_node[14], pull_resistor_13_node[15], pull_resistor_15_node[4], pull_resistor_15_node[5], pull_resistor_15_node[6], pull_resistor_15_node[7], pull_resistor_15_node[8], pull_resistor_15_node[9], pull_resistor_15_node[10], pull_resistor_15_node[11], pull_resistor_15_node[12], pull_resistor_15_node[13], pull_resistor_15_node[14], pull_resistor_15_node[15], pull_resistor_17_node[4], pull_resistor_17_node[5], pull_resistor_17_node[6], pull_resistor_17_node[7], pull_resistor_17_node[8], pull_resistor_17_node[9], pull_resistor_17_node[10], pull_resistor_17_node[11], pull_resistor_17_node[12], pull_resistor_17_node[13], pull_resistor_17_node[14], pull_resistor_17_node[15], controlled_buffer_39_out[0], controlled_buffer_39_out[1], controlled_buffer_39_out[2], controlled_buffer_39_out[3], controlled_buffer_39_out[4], controlled_buffer_39_out[5], controlled_buffer_39_out[6], controlled_buffer_39_out[7], controlled_buffer_39_out[8], controlled_buffer_39_out[9], controlled_buffer_39_out[10], controlled_buffer_39_out[11], controlled_buffer_39_out[12], controlled_buffer_39_out[13], controlled_buffer_39_out[14], controlled_buffer_39_out[15]}

  // Other names for the same wires on the sheet: HI_LO_DIR_WR = HILO_DIR_WR; INSTRUCTION_CONTENTS[9:0] = DATA;
  //   lowr_1[15:0] = hiwr_0; OUTPUT_DATA[15:0] = hiwr_0; OUT_0_ADDR[4:0] = OUTPUT_0_ADDR; OUT_0_DATA[15:0] = OUTPUT_0;
  //   OUT_1_ADDR[4:0] = OUTPUT_1_ADDR; OUT_1_DATA[15:0] = OUTPUT_1; REGISTER_0_DATA[15:0] = INPUT_0;
  //   REGISTER_1_DATA[15:0] = INPUT_1; op_addr_0[4:0] = READ_0_ADDR; result_output_addr[4:0] = READ_0_ADDR;
  //   op_addr_1[4:0] = READ_1_ADDR; result_output_addr_1[4:0] = READ_1_ADDR

  // Notes on the sheet:
  //   INPUT_0: pull=down
  //   INPUT_1: pull=down
  //   ALU Input Range: 0x00 - 0x19
  //   Immediate Instruction Flag
  //   Long Immediate Flag
endmodule

module REGISTERS (
  input  [15:0] CARRY_DIR_IN,
  input  clk_in,
  input  CARRY_DIR_WR,
  input  SYS_RESET,
  input  HI_LO_WR,
  input  CMP_DIR_IN,
  input  CMP_DIR_WR,
  input  [15:0] HI_IN,
  input  [15:0] LO_IN,
  input  [4:0] READ_1,
  input  [4:0] READ_0,
  input  [4:0] WRITE_0,
  input  [4:0] WRITE_1,
  input  [15:0] DATA_IN_0,
  input  [15:0] DATA_IN_1,
  output [15:0] OUTPUT_0,
  output [15:0] SP_OUT,
  output [15:0] GPR0_OUT,
  output [15:0] OUTPUT_1,
  output [15:0] CMP_DIR_OUT,
  output [15:0] PC_OUT,
  output CARRY_DIR_OUT
);

  wire buffer_1_out, buffer_2_out, buffer_3_out, buffer_5_out, buffer_7_out, buffer_9_out, buffer_11_out,
       buffer_13_out, buffer_15_out, buffer_17_out, buffer_19_out, buffer_21_out, buffer_23_out,
       buffer_25_out, buffer_27_out, buffer_29_out, buffer_31_out, buffer_33_out, buffer_35_out,
       buffer_37_out, buffer_39_out, buffer_41_out, buffer_43_out, buffer_45_out, buffer_47_out,
       buffer_49_out, buffer_51_out, buffer_53_out, buffer_55_out, counter_1_carry, demultiplexer_2_out0,
       R_0_0, R_0_1, R_0_2, R_0_3, R_0_4, R_0_5, R_0_6, R_0_7, R_0_8, R_0_9, R_0_10, R_0_11, R_0_12, R_0_13,
       R_0_14, R_0_15, R_0_16, R_0_17, R_0_18, R_0_19, R_0_20, R_0_21, R_0_22, R_0_23, R_0_24, R_0_25,
       R_0_26, R_0_27, R_0_28, R_0_29, R_0_30, R_0_31, R_1_0, R_1_1, R_1_2, R_1_3, R_1_4, R_1_5, R_1_6,
       R_1_7, R_1_8, R_1_9, R_1_10, R_1_11, R_1_12, R_1_13, R_1_14, R_1_15, R_1_16, R_1_17, R_1_18, R_1_19,
       R_1_20, R_1_21, R_1_22, R_1_23, R_1_24, R_1_25, R_1_26, R_1_27, R_1_28, R_1_29, R_1_30, R_1_31, W_0,
       W_0_1, W_1, W_1_1, W_2, W_2_1, W_3, W_3_1, W_4, W_4_1, W_5, W_5_1, W_6, W_6_1, W_7, W_7_1, W_8, W_8_1,
       W_9, W_9_1, W_25, W_25_1, W_26, W_26_1, W_27, W_27_1, W_28, W_28_1, W_29, W_29_1, W_30, W_30_1, W_A,
       W_A_1, W_B, W_B_1, W_CMP, W_CMP_1, W_HI, W_HI_1, W_INTER_FIELD, W_INTER_FIELD_1, W_LO, W_LO_1, W_NULL,
       W_PC, W_PC_1, W_RA, W_RA_1, W_SP, W_SP_1, W_SYSTICK_HI, W_SYSTICK_HI_1, W_SYSTICK_LO, W_SYSTICK_LO_1,
       W_USR_CLK_0, W_USR_CLK_0_1, W_USR_CLK_1, W_USR_CLK_1_1, W_USR_CLK_2, W_USR_CLK_2_1, W_USR_CLK_3,
       W_USR_CLK_3_1;
  wire [15:0] controlled_buffer_1_out, controlled_buffer_2_out, controlled_buffer_3_out,
       controlled_buffer_5_out, controlled_buffer_7_out, controlled_buffer_9_out, controlled_buffer_11_out,
       controlled_buffer_13_out, controlled_buffer_15_out, controlled_buffer_17_out,
       controlled_buffer_19_out, controlled_buffer_21_out, controlled_buffer_23_out,
       controlled_buffer_25_out, controlled_buffer_27_out, controlled_buffer_29_out,
       controlled_buffer_31_out, controlled_buffer_33_out, controlled_buffer_35_out,
       controlled_buffer_37_out, controlled_buffer_39_out, controlled_buffer_41_out,
       controlled_buffer_43_out, controlled_buffer_45_out, controlled_buffer_47_out,
       controlled_buffer_49_out, controlled_buffer_51_out, controlled_buffer_53_out, GPR1_OUT, GPR2_OUT,
       GPR3_OUT, GPR4_OUT, GPR5_OUT, GPR6_OUT, GPR7_OUT, GPR8_OUT, GPR9_OUT, GPRA_OUT, GPRB_OUT, hi_out,
       interField, lo_out, ra, register_24_q, register_25_q, register_26_q, register_27_q, register_28_q,
       register_29_q, systick_hi_in, systick_hi_out, systick_lo_in, systick_lo_out, usr_clk0_out,
       usr_clk1_out, usr_clk2_out, usr_clk3_out;

  Counter #(.width(16), .max('hffff)) counter_1 (
    .Q(systick_lo_in), .carry(counter_1_carry), .clk(clk_in));  // open: load, D, count, clr
  Counter #(.width(16), .max('hffff)) counter_2 (
    .Q(systick_hi_in), .clk(counter_1_carry));  // open: load, D, count, carry, clr
  Pull_Resistor pull_resistor_1 (.node(HI_LO_WR));
  Demultiplexer #(.select(5), .disabled(0)) demultiplexer_1 (
    .out0(R_0_0), .out1(R_0_1), .out2(R_0_2), .out3(R_0_3), .out4(R_0_4), .out5(R_0_5), .out6(R_0_6),
    .out7(R_0_7), .out8(R_0_8), .out9(R_0_9), .out10(R_0_10), .out11(R_0_11), .out12(R_0_12), .out13(R_0_13),
    .out14(R_0_14), .out15(R_0_15), .out16(R_0_16), .out17(R_0_17), .out18(R_0_18), .out19(R_0_19),
    .out20(R_0_20), .out21(R_0_21), .out22(R_0_22), .out23(R_0_23), .out24(R_0_24), .out25(R_0_25),
    .out26(R_0_26), .out27(R_0_27), .out28(R_0_28), .out29(R_0_29), .out30(R_0_30), .out31(R_0_31),
    .in(1'b1), .sel(READ_0), .en(1'b1));
  Demultiplexer #(.select(5), .disabled(0)) demultiplexer_2 (
    .out0(demultiplexer_2_out0), .out1(W_0), .out2(W_1), .out3(W_2), .out4(W_3), .out5(W_4), .out6(W_5),
    .out7(W_6), .out8(W_7), .out9(W_8), .out10(W_9), .out11(W_A), .out12(W_B), .out13(W_PC), .out14(W_RA),
    .out15(W_SP), .out16(W_CMP), .out17(W_HI), .out18(W_LO), .out19(W_SYSTICK_HI), .out20(W_SYSTICK_LO),
    .out21(W_USR_CLK_0), .out22(W_USR_CLK_1), .out23(W_USR_CLK_2), .out24(W_USR_CLK_3), .out25(W_25),
    .out26(W_26), .out27(W_27), .out28(W_28), .out29(W_29), .out30(W_30), .out31(W_INTER_FIELD), .in(1'b1),
    .sel(WRITE_0), .en(1'b1));
  assign controlled_buffer_1_out = HI_LO_WR ? HI_IN : 16'bz;  // Controlled_Buffer controlled_buffer_1
  buf buffer_1 (buffer_1_out, HI_LO_WR);
  assign controlled_buffer_2_out = HI_LO_WR ? LO_IN : 16'bz;  // Controlled_Buffer controlled_buffer_2
  buf buffer_2 (buffer_2_out, HI_LO_WR);
  Pull_Resistor pull_resistor_2 (.node(READ_1));
  Pull_Resistor pull_resistor_3 (.node(WRITE_1));
  assign controlled_buffer_3_out = W_0 ? DATA_IN_0 : 16'bz;  // Controlled_Buffer controlled_buffer_3
  assign controlled_buffer_3_out = W_0_1 ? DATA_IN_1 : 16'bz;  // Controlled_Buffer controlled_buffer_4
  assign controlled_buffer_5_out = W_1 ? DATA_IN_0 : 16'bz;  // Controlled_Buffer controlled_buffer_5
  assign controlled_buffer_5_out = W_1_1 ? DATA_IN_1 : 16'bz;  // Controlled_Buffer controlled_buffer_6
  assign controlled_buffer_7_out = W_2 ? DATA_IN_0 : 16'bz;  // Controlled_Buffer controlled_buffer_7
  assign controlled_buffer_7_out = W_2_1 ? DATA_IN_1 : 16'bz;  // Controlled_Buffer controlled_buffer_8
  assign controlled_buffer_9_out = W_3 ? DATA_IN_0 : 16'bz;  // Controlled_Buffer controlled_buffer_9
  assign controlled_buffer_9_out = W_3_1 ? DATA_IN_1 : 16'bz;  // Controlled_Buffer controlled_buffer_10
  assign controlled_buffer_11_out = W_4 ? DATA_IN_0 : 16'bz;  // Controlled_Buffer controlled_buffer_11
  assign controlled_buffer_11_out = W_4_1 ? DATA_IN_1 : 16'bz;  // Controlled_Buffer controlled_buffer_12
  assign controlled_buffer_13_out = W_5 ? DATA_IN_0 : 16'bz;  // Controlled_Buffer controlled_buffer_13
  assign controlled_buffer_13_out = W_5_1 ? DATA_IN_1 : 16'bz;  // Controlled_Buffer controlled_buffer_14
  assign controlled_buffer_15_out = W_6 ? DATA_IN_0 : 16'bz;  // Controlled_Buffer controlled_buffer_15
  assign controlled_buffer_15_out = W_6_1 ? DATA_IN_1 : 16'bz;  // Controlled_Buffer controlled_buffer_16
  assign controlled_buffer_17_out = W_7 ? DATA_IN_0 : 16'bz;  // Controlled_Buffer controlled_buffer_17
  assign controlled_buffer_17_out = W_7_1 ? DATA_IN_1 : 16'bz;  // Controlled_Buffer controlled_buffer_18
  assign controlled_buffer_19_out = W_8 ? DATA_IN_0 : 16'bz;  // Controlled_Buffer controlled_buffer_19
  assign controlled_buffer_19_out = W_8_1 ? DATA_IN_1 : 16'bz;  // Controlled_Buffer controlled_buffer_20
  assign controlled_buffer_21_out = W_9 ? DATA_IN_0 : 16'bz;  // Controlled_Buffer controlled_buffer_21
  assign controlled_buffer_21_out = W_9_1 ? DATA_IN_1 : 16'bz;  // Controlled_Buffer controlled_buffer_22
  assign controlled_buffer_23_out = W_A ? DATA_IN_0 : 16'bz;  // Controlled_Buffer controlled_buffer_23
  assign controlled_buffer_23_out = W_A_1 ? DATA_IN_1 : 16'bz;  // Controlled_Buffer controlled_buffer_24
  assign controlled_buffer_25_out = W_B ? DATA_IN_0 : 16'bz;  // Controlled_Buffer controlled_buffer_25
  assign controlled_buffer_25_out = W_B_1 ? DATA_IN_1 : 16'bz;  // Controlled_Buffer controlled_buffer_26
  assign controlled_buffer_27_out = W_RA ? DATA_IN_0 : 16'bz;  // Controlled_Buffer controlled_buffer_27
  assign controlled_buffer_27_out = W_RA_1 ? DATA_IN_1 : 16'bz;  // Controlled_Buffer controlled_buffer_28
  buf buffer_3 (buffer_3_out, W_PC);
  buf buffer_4 (buffer_3_out, W_PC_1);
  assign controlled_buffer_29_out = W_SP ? DATA_IN_0 : 16'bz;  // Controlled_Buffer controlled_buffer_29
  assign controlled_buffer_29_out = W_SP_1 ? DATA_IN_1 : 16'bz;  // Controlled_Buffer controlled_buffer_30
  assign controlled_buffer_31_out = W_CMP ? DATA_IN_0 : 16'bz;  // Controlled_Buffer controlled_buffer_31
  assign controlled_buffer_31_out = W_CMP_1 ? DATA_IN_1 : 16'bz;  // Controlled_Buffer controlled_buffer_32
  assign controlled_buffer_33_out = W_USR_CLK_0 ? DATA_IN_0 : 16'bz;  // Controlled_Buffer controlled_buffer_33
  assign controlled_buffer_33_out = W_USR_CLK_0_1 ? DATA_IN_1 : 16'bz;  // Controlled_Buffer controlled_buffer_34
  assign controlled_buffer_35_out = W_USR_CLK_1 ? DATA_IN_0 : 16'bz;  // Controlled_Buffer controlled_buffer_35
  assign controlled_buffer_35_out = W_USR_CLK_1_1 ? DATA_IN_1 : 16'bz;  // Controlled_Buffer controlled_buffer_36
  assign controlled_buffer_37_out = W_USR_CLK_2 ? DATA_IN_0 : 16'bz;  // Controlled_Buffer controlled_buffer_37
  assign controlled_buffer_37_out = W_USR_CLK_2_1 ? DATA_IN_1 : 16'bz;  // Controlled_Buffer controlled_buffer_38
  assign controlled_buffer_39_out = W_USR_CLK_3 ? DATA_IN_0 : 16'bz;  // Controlled_Buffer controlled_buffer_39
  assign controlled_buffer_39_out = W_USR_CLK_3_1 ? DATA_IN_1 : 16'bz;  // Controlled_Buffer controlled_buffer_40
  assign controlled_buffer_41_out = W_25 ? DATA_IN_0 : 16'bz;  // Controlled_Buffer controlled_buffer_41
  assign controlled_buffer_41_out = W_25_1 ? DATA_IN_1 : 16'bz;  // Controlled_Buffer controlled_buffer_42
  assign controlled_buffer_43_out = W_26 ? DATA_IN_0 : 16'bz;  // Controlled_Buffer controlled_buffer_43
  assign controlled_buffer_43_out = W_26_1 ? DATA_IN_1 : 16'bz;  // Controlled_Buffer controlled_buffer_44
  assign controlled_buffer_45_out = W_27 ? DATA_IN_0 : 16'bz;  // Controlled_Buffer controlled_buffer_45
  assign controlled_buffer_45_out = W_27_1 ? DATA_IN_1 : 16'bz;  // Controlled_Buffer controlled_buffer_46
  assign controlled_buffer_47_out = W_28 ? DATA_IN_0 : 16'bz;  // Controlled_Buffer controlled_buffer_47
  assign controlled_buffer_47_out = W_28_1 ? DATA_IN_1 : 16'bz;  // Controlled_Buffer controlled_buffer_48
  assign controlled_buffer_49_out = W_29 ? DATA_IN_0 : 16'bz;  // Controlled_Buffer controlled_buffer_49
  assign controlled_buffer_49_out = W_29_1 ? DATA_IN_1 : 16'bz;  // Controlled_Buffer controlled_buffer_50
  assign controlled_buffer_51_out = W_30 ? DATA_IN_0 : 16'bz;  // Controlled_Buffer controlled_buffer_51
  assign controlled_buffer_51_out = W_30_1 ? DATA_IN_1 : 16'bz;  // Controlled_Buffer controlled_buffer_52
  assign controlled_buffer_53_out = W_INTER_FIELD ? DATA_IN_0 : 16'bz;  // Controlled_Buffer controlled_buffer_53
  assign controlled_buffer_53_out = W_INTER_FIELD_1 ? DATA_IN_1 : 16'bz;  // Controlled_Buffer controlled_buffer_54
  buf buffer_5 (buffer_5_out, W_0);
  buf buffer_6 (buffer_5_out, W_0_1);
  buf buffer_7 (buffer_7_out, W_1);
  buf buffer_8 (buffer_7_out, W_1_1);
  buf buffer_9 (buffer_9_out, W_2);
  buf buffer_10 (buffer_9_out, W_2_1);
  buf buffer_11 (buffer_11_out, W_3);
  buf buffer_12 (buffer_11_out, W_3_1);
  buf buffer_13 (buffer_13_out, W_4);
  buf buffer_14 (buffer_13_out, W_4_1);
  buf buffer_15 (buffer_15_out, W_5);
  buf buffer_16 (buffer_15_out, W_5_1);
  buf buffer_17 (buffer_17_out, W_6);
  buf buffer_18 (buffer_17_out, W_6_1);
  buf buffer_19 (buffer_19_out, W_7);
  buf buffer_20 (buffer_19_out, W_7_1);
  buf buffer_21 (buffer_21_out, W_8);
  buf buffer_22 (buffer_21_out, W_8_1);
  buf buffer_23 (buffer_23_out, W_9);
  buf buffer_24 (buffer_23_out, W_9_1);
  buf buffer_25 (buffer_25_out, W_A);
  buf buffer_26 (buffer_25_out, W_A_1);
  buf buffer_27 (buffer_27_out, W_B);
  buf buffer_28 (buffer_27_out, W_B_1);
  buf buffer_29 (buffer_29_out, W_RA);
  buf buffer_30 (buffer_29_out, W_RA_1);
  buf buffer_31 (buffer_31_out, W_SP);
  buf buffer_32 (buffer_31_out, W_SP_1);
  buf buffer_33 (buffer_33_out, W_CMP);
  buf buffer_34 (buffer_33_out, W_CMP_1);
  buf buffer_35 (buffer_35_out, W_USR_CLK_0);
  buf buffer_36 (buffer_35_out, W_USR_CLK_0_1);
  buf buffer_37 (buffer_37_out, W_USR_CLK_1);
  buf buffer_38 (buffer_37_out, W_USR_CLK_1_1);
  buf buffer_39 (buffer_39_out, W_USR_CLK_2);
  buf buffer_40 (buffer_39_out, W_USR_CLK_2_1);
  buf buffer_41 (buffer_41_out, W_USR_CLK_3);
  buf buffer_42 (buffer_41_out, W_USR_CLK_3_1);
  buf buffer_43 (buffer_43_out, W_25);
  buf buffer_44 (buffer_43_out, W_25_1);
  buf buffer_45 (buffer_45_out, W_26);
  buf buffer_46 (buffer_45_out, W_26_1);
  buf buffer_47 (buffer_47_out, W_27);
  buf buffer_48 (buffer_47_out, W_27_1);
  buf buffer_49 (buffer_49_out, W_28);
  buf buffer_50 (buffer_49_out, W_28_1);
  buf buffer_51 (buffer_51_out, W_29);
  buf buffer_52 (buffer_51_out, W_29_1);
  buf buffer_53 (buffer_53_out, W_30);
  buf buffer_54 (buffer_53_out, W_30_1);
  buf buffer_55 (buffer_55_out, W_INTER_FIELD);
  buf buffer_56 (buffer_55_out, W_INTER_FIELD_1);
  Pull_Resistor pull_resistor_4 (.node(OUTPUT_0));
  Pull_Resistor pull_resistor_5 (.node(OUTPUT_1));
  Demultiplexer #(.select(5), .disabled(0)) demultiplexer_3 (
    .out0(R_1_0), .out1(R_1_1), .out2(R_1_2), .out3(R_1_3), .out4(R_1_4), .out5(R_1_5), .out6(R_1_6),
    .out7(R_1_7), .out8(R_1_8), .out9(R_1_9), .out10(R_1_10), .out11(R_1_11), .out12(R_1_12), .out13(R_1_13),
    .out14(R_1_14), .out15(R_1_15), .out16(R_1_16), .out17(R_1_17), .out18(R_1_18), .out19(R_1_19),
    .out20(R_1_20), .out21(R_1_21), .out22(R_1_22), .out23(R_1_23), .out24(R_1_24), .out25(R_1_25),
    .out26(R_1_26), .out27(R_1_27), .out28(R_1_28), .out29(R_1_29), .out30(R_1_30), .out31(R_1_31),
    .in(1'b1), .sel(READ_1), .en(1'b1));
  Demultiplexer #(.select(5), .disabled(0)) demultiplexer_4 (
    .out0(W_NULL), .out1(W_0_1), .out2(W_1_1), .out3(W_2_1), .out4(W_3_1), .out5(W_4_1), .out6(W_5_1),
    .out7(W_6_1), .out8(W_7_1), .out9(W_8_1), .out10(W_9_1), .out11(W_A_1), .out12(W_B_1), .out13(W_PC_1),
    .out14(W_RA_1), .out15(W_SP_1), .out16(W_CMP_1), .out17(W_HI_1), .out18(W_LO_1), .out19(W_SYSTICK_HI_1),
    .out20(W_SYSTICK_LO_1), .out21(W_USR_CLK_0_1), .out22(W_USR_CLK_1_1), .out23(W_USR_CLK_2_1),
    .out24(W_USR_CLK_3_1), .out25(W_25_1), .out26(W_26_1), .out27(W_27_1), .out28(W_28_1), .out29(W_29_1),
    .out30(W_30_1), .out31(W_INTER_FIELD_1), .in(1'b1), .sel(WRITE_1), .en(1'b1));
  Register #(.width(16), .trigger("falling")) register_1 (
    .D(controlled_buffer_3_out), .en(buffer_5_out), .Q(GPR0_OUT), .clk(clk_in), .clr(SYS_RESET));
  Register #(.width(16), .trigger("falling")) register_2 (
    .D(controlled_buffer_5_out), .en(buffer_7_out), .Q(GPR1_OUT), .clk(clk_in), .clr(SYS_RESET));
  Register #(.width(16), .trigger("falling")) register_3 (
    .D(controlled_buffer_7_out), .en(buffer_9_out), .Q(GPR2_OUT), .clk(clk_in), .clr(SYS_RESET));
  Register #(.width(16), .trigger("falling")) register_4 (
    .D(controlled_buffer_9_out), .en(buffer_11_out), .Q(GPR3_OUT), .clk(clk_in), .clr(SYS_RESET));
  Register #(.width(16), .trigger("falling")) register_5 (
    .D(controlled_buffer_11_out), .en(buffer_13_out), .Q(GPR4_OUT), .clk(clk_in), .clr(SYS_RESET));
  Register #(.width(16), .trigger("falling")) register_6 (
    .D(controlled_buffer_13_out), .en(buffer_15_out), .Q(GPR5_OUT), .clk(clk_in), .clr(SYS_RESET));
  Register #(.width(16), .trigger("falling")) register_7 (
    .D(controlled_buffer_15_out), .en(buffer_17_out), .Q(GPR6_OUT), .clk(clk_in), .clr(SYS_RESET));
  Register #(.width(16), .trigger("falling")) register_8 (
    .D(controlled_buffer_17_out), .en(buffer_19_out), .Q(GPR7_OUT), .clk(clk_in), .clr(SYS_RESET));
  Register #(.width(16), .trigger("falling")) register_9 (
    .D(controlled_buffer_19_out), .en(buffer_21_out), .Q(GPR8_OUT), .clk(clk_in), .clr(SYS_RESET));
  Register #(.width(16), .trigger("falling")) register_10 (
    .D(controlled_buffer_21_out), .en(buffer_23_out), .Q(GPR9_OUT), .clk(clk_in), .clr(SYS_RESET));
  Register #(.width(16), .trigger("falling")) register_11 (
    .D(controlled_buffer_23_out), .en(buffer_25_out), .Q(GPRA_OUT), .clk(clk_in), .clr(SYS_RESET));
  Register #(.width(16), .trigger("falling")) register_12 (
    .D(controlled_buffer_25_out), .en(buffer_27_out), .Q(GPRB_OUT), .clk(clk_in), .clr(SYS_RESET));
  Register #(.width(16), .trigger("falling")) register_13 (
    .D(controlled_buffer_27_out), .en(buffer_29_out), .Q(ra), .clk(clk_in), .clr(SYS_RESET));
  Counter #(.width(16), .max('hffff)) counter_3 (
    .load(buffer_3_out), .D(ra), .Q(PC_OUT), .clk(clk_in), .clr(SYS_RESET));  // open: count, carry
  Pull_Resistor pull_resistor_6 (.node(SYS_RESET));
  Register #(.width(16), .trigger("falling")) register_14 (
    .D(controlled_buffer_29_out), .en(buffer_31_out), .Q(SP_OUT), .clk(clk_in), .clr(SYS_RESET));
  Register #(.width(16), .trigger("falling")) register_15 (
    .D(controlled_buffer_31_out), .en(buffer_33_out), .Q(CMP_DIR_OUT), .clk(clk_in), .clr(SYS_RESET));
  Register #(.width(16)) register_16 (
    .D(controlled_buffer_1_out), .en(buffer_1_out), .Q(hi_out), .clk(clk_in), .clr(SYS_RESET));
  Register #(.width(16)) register_17 (
    .D(controlled_buffer_2_out), .en(buffer_2_out), .Q(lo_out), .clk(clk_in), .clr(SYS_RESET));
  Register #(.width(16), .trigger("high")) register_18 (
    .D(systick_hi_in), .en(1'b1), .Q(systick_hi_out), .clk(clk_in), .clr(SYS_RESET));
  Register #(.width(16), .trigger("high")) register_19 (
    .D(systick_lo_in), .en(1'b1), .Q(systick_lo_out), .clk(clk_in), .clr(SYS_RESET));
  Register #(.width(16)) register_20 (
    .D(controlled_buffer_33_out), .en(buffer_35_out), .Q(usr_clk0_out), .clk(clk_in), .clr(SYS_RESET));
  Register #(.width(16)) register_21 (
    .D(controlled_buffer_35_out), .en(buffer_37_out), .Q(usr_clk1_out), .clk(clk_in), .clr(SYS_RESET));
  Register #(.width(16)) register_22 (
    .D(controlled_buffer_37_out), .en(buffer_39_out), .Q(usr_clk2_out), .clk(clk_in), .clr(SYS_RESET));
  Register #(.width(16)) register_23 (
    .D(controlled_buffer_39_out), .en(buffer_41_out), .Q(usr_clk3_out), .clk(clk_in), .clr(SYS_RESET));
  Register #(.width(16)) register_24 (
    .D(controlled_buffer_41_out), .en(buffer_43_out), .Q(register_24_q), .clk(clk_in), .clr(SYS_RESET));
  Register #(.width(16)) register_25 (
    .D(controlled_buffer_43_out), .en(buffer_45_out), .Q(register_25_q), .clk(clk_in), .clr(SYS_RESET));
  Register #(.width(16)) register_26 (
    .D(controlled_buffer_45_out), .en(buffer_47_out), .Q(register_26_q), .clk(clk_in), .clr(SYS_RESET));
  Register #(.width(16)) register_27 (
    .D(controlled_buffer_47_out), .en(buffer_49_out), .Q(register_27_q), .clk(clk_in), .clr(SYS_RESET));
  Register #(.width(16)) register_28 (
    .D(controlled_buffer_49_out), .en(buffer_51_out), .Q(register_28_q), .clk(clk_in), .clr(SYS_RESET));
  Register #(.width(16)) register_29 (
    .D(controlled_buffer_51_out), .en(buffer_53_out), .Q(register_29_q), .clk(clk_in), .clr(SYS_RESET));
  Register #(.width(16)) register_30 (
    .D(controlled_buffer_53_out), .en(buffer_55_out), .Q(interField), .clk(clk_in), .clr(SYS_RESET));
  assign OUTPUT_0 = R_0_0 ? {16{1'b0}} : 16'bz;  // Controlled_Buffer controlled_buffer_55
  assign OUTPUT_0 = R_0_1 ? GPR0_OUT : 16'bz;  // Controlled_Buffer controlled_buffer_56
  assign OUTPUT_0 = R_0_2 ? GPR1_OUT : 16'bz;  // Controlled_Buffer controlled_buffer_57
  assign OUTPUT_0 = R_0_3 ? GPR2_OUT : 16'bz;  // Controlled_Buffer controlled_buffer_58
  assign OUTPUT_0 = R_0_4 ? GPR3_OUT : 16'bz;  // Controlled_Buffer controlled_buffer_59
  assign OUTPUT_0 = R_0_5 ? GPR4_OUT : 16'bz;  // Controlled_Buffer controlled_buffer_60
  assign OUTPUT_0 = R_0_6 ? GPR5_OUT : 16'bz;  // Controlled_Buffer controlled_buffer_61
  assign OUTPUT_0 = R_0_7 ? GPR6_OUT : 16'bz;  // Controlled_Buffer controlled_buffer_62
  assign OUTPUT_0 = R_0_8 ? GPR7_OUT : 16'bz;  // Controlled_Buffer controlled_buffer_63
  assign OUTPUT_0 = R_0_9 ? GPR8_OUT : 16'bz;  // Controlled_Buffer controlled_buffer_64
  assign OUTPUT_0 = R_0_10 ? GPR9_OUT : 16'bz;  // Controlled_Buffer controlled_buffer_65
  assign OUTPUT_0 = R_0_11 ? GPRA_OUT : 16'bz;  // Controlled_Buffer controlled_buffer_66
  assign OUTPUT_0 = R_0_12 ? GPRB_OUT : 16'bz;  // Controlled_Buffer controlled_buffer_67
  assign OUTPUT_0 = R_0_13 ? ra : 16'bz;  // Controlled_Buffer controlled_buffer_68
  assign OUTPUT_0 = R_0_14 ? PC_OUT : 16'bz;  // Controlled_Buffer controlled_buffer_69
  assign OUTPUT_0 = R_0_15 ? SP_OUT : 16'bz;  // Controlled_Buffer controlled_buffer_70
  assign OUTPUT_0 = R_0_16 ? CMP_DIR_OUT : 16'bz;  // Controlled_Buffer controlled_buffer_71
  assign OUTPUT_0 = R_0_17 ? hi_out : 16'bz;  // Controlled_Buffer controlled_buffer_72
  assign OUTPUT_0 = R_0_18 ? lo_out : 16'bz;  // Controlled_Buffer controlled_buffer_73
  assign OUTPUT_0 = R_0_19 ? systick_hi_out : 16'bz;  // Controlled_Buffer controlled_buffer_74
  assign OUTPUT_0 = R_0_20 ? systick_lo_out : 16'bz;  // Controlled_Buffer controlled_buffer_75
  assign OUTPUT_0 = R_0_21 ? usr_clk0_out : 16'bz;  // Controlled_Buffer controlled_buffer_76
  assign OUTPUT_0 = R_0_22 ? usr_clk1_out : 16'bz;  // Controlled_Buffer controlled_buffer_77
  assign OUTPUT_0 = R_0_23 ? usr_clk2_out : 16'bz;  // Controlled_Buffer controlled_buffer_78
  assign OUTPUT_0 = R_0_24 ? usr_clk3_out : 16'bz;  // Controlled_Buffer controlled_buffer_79
  assign OUTPUT_0 = R_0_25 ? register_24_q : 16'bz;  // Controlled_Buffer controlled_buffer_80
  assign OUTPUT_0 = R_0_26 ? register_25_q : 16'bz;  // Controlled_Buffer controlled_buffer_81
  assign OUTPUT_0 = R_0_27 ? register_26_q : 16'bz;  // Controlled_Buffer controlled_buffer_82
  assign OUTPUT_0 = R_0_28 ? register_27_q : 16'bz;  // Controlled_Buffer controlled_buffer_83
  assign OUTPUT_0 = R_0_29 ? register_28_q : 16'bz;  // Controlled_Buffer controlled_buffer_84
  assign OUTPUT_0 = R_0_30 ? register_29_q : 16'bz;  // Controlled_Buffer controlled_buffer_85
  assign OUTPUT_0 = R_0_31 ? interField : 16'bz;  // Controlled_Buffer controlled_buffer_86
  assign OUTPUT_1 = R_1_0 ? {16{1'b0}} : 16'bz;  // Controlled_Buffer controlled_buffer_87
  assign OUTPUT_1 = R_1_1 ? GPR0_OUT : 16'bz;  // Controlled_Buffer controlled_buffer_88
  assign OUTPUT_1 = R_1_2 ? GPR1_OUT : 16'bz;  // Controlled_Buffer controlled_buffer_89
  assign OUTPUT_1 = R_1_3 ? GPR2_OUT : 16'bz;  // Controlled_Buffer controlled_buffer_90
  assign OUTPUT_1 = R_1_4 ? GPR3_OUT : 16'bz;  // Controlled_Buffer controlled_buffer_91
  assign OUTPUT_1 = R_1_5 ? GPR4_OUT : 16'bz;  // Controlled_Buffer controlled_buffer_92
  assign OUTPUT_1 = R_1_6 ? GPR5_OUT : 16'bz;  // Controlled_Buffer controlled_buffer_93
  assign OUTPUT_1 = R_1_7 ? GPR6_OUT : 16'bz;  // Controlled_Buffer controlled_buffer_94
  assign OUTPUT_1 = R_1_8 ? GPR7_OUT : 16'bz;  // Controlled_Buffer controlled_buffer_95
  assign OUTPUT_1 = R_1_9 ? GPR8_OUT : 16'bz;  // Controlled_Buffer controlled_buffer_96
  assign OUTPUT_1 = R_1_10 ? GPR9_OUT : 16'bz;  // Controlled_Buffer controlled_buffer_97
  assign OUTPUT_1 = R_1_11 ? GPRA_OUT : 16'bz;  // Controlled_Buffer controlled_buffer_98
  assign OUTPUT_1 = R_1_12 ? GPRB_OUT : 16'bz;  // Controlled_Buffer controlled_buffer_99
  assign OUTPUT_1 = R_1_13 ? ra : 16'bz;  // Controlled_Buffer controlled_buffer_100
  assign OUTPUT_1 = R_1_14 ? PC_OUT : 16'bz;  // Controlled_Buffer controlled_buffer_101
  assign OUTPUT_1 = R_1_15 ? SP_OUT : 16'bz;  // Controlled_Buffer controlled_buffer_102
  assign OUTPUT_1 = R_1_16 ? CMP_DIR_OUT : 16'bz;  // Controlled_Buffer controlled_buffer_103
  assign OUTPUT_1 = R_1_17 ? hi_out : 16'bz;  // Controlled_Buffer controlled_buffer_104
  assign OUTPUT_1 = R_1_18 ? lo_out : 16'bz;  // Controlled_Buffer controlled_buffer_105
  assign OUTPUT_1 = R_1_19 ? systick_hi_out : 16'bz;  // Controlled_Buffer controlled_buffer_106
  assign OUTPUT_1 = R_1_20 ? systick_lo_out : 16'bz;  // Controlled_Buffer controlled_buffer_107
  assign OUTPUT_1 = R_1_21 ? usr_clk0_out : 16'bz;  // Controlled_Buffer controlled_buffer_108
  assign OUTPUT_1 = R_1_22 ? usr_clk1_out : 16'bz;  // Controlled_Buffer controlled_buffer_109
  assign OUTPUT_1 = R_1_23 ? usr_clk2_out : 16'bz;  // Controlled_Buffer controlled_buffer_110
  assign OUTPUT_1 = R_1_24 ? usr_clk3_out : 16'bz;  // Controlled_Buffer controlled_buffer_111
  assign OUTPUT_1 = R_1_25 ? register_24_q : 16'bz;  // Controlled_Buffer controlled_buffer_112
  assign OUTPUT_1 = R_1_26 ? register_25_q : 16'bz;  // Controlled_Buffer controlled_buffer_113
  assign OUTPUT_1 = R_1_27 ? register_26_q : 16'bz;  // Controlled_Buffer controlled_buffer_114
  assign OUTPUT_1 = R_1_28 ? register_27_q : 16'bz;  // Controlled_Buffer controlled_buffer_115
  assign OUTPUT_1 = R_1_29 ? register_28_q : 16'bz;  // Controlled_Buffer controlled_buffer_116
  assign OUTPUT_1 = R_1_30 ? register_29_q : 16'bz;  // Controlled_Buffer controlled_buffer_117
  assign OUTPUT_1 = R_1_31 ? interField : 16'bz;  // Controlled_Buffer controlled_buffer_118

  assign CARRY_DIR_OUT = 1'b0;
  // also tied to GND on the sheet: {CARRY_DIR_IN[0], CARRY_DIR_IN[1], CARRY_DIR_IN[2], CARRY_DIR_IN[3], CARRY_DIR_IN[4], CARRY_DIR_IN[5], CARRY_DIR_IN[6], CARRY_DIR_IN[7], CARRY_DIR_IN[8], CARRY_DIR_IN[9], CARRY_DIR_IN[10], CARRY_DIR_IN[11], CARRY_DIR_IN[12], CARRY_DIR_IN[13], CARRY_DIR_IN[14], CARRY_DIR_IN[15], CARRY_DIR_WR, CMP_DIR_WR, CMP_DIR_IN}

  // Other names for the same wires on the sheet: CARRY_IN_DIR[15:0] = CARRY_DIR_IN; CARRY_IN_WR = CARRY_DIR_WR;
  //   CMP_IN_DIR = CMP_DIR_WR; CMP_IN_WR = CMP_DIR_IN; cmp_out[15:0] = CMP_DIR_OUT; DIN_0[15:0] = DATA_IN_0;
  //   DIN_1[15:0] = DATA_IN_1; HI_WR_DIR[15:0] = HI_IN; HILO_WR = HI_LO_WR; LO_WR_DIR[15:0] = LO_IN;
  //   OUT0[15:0] = OUTPUT_0; OUT1[15:0] = OUTPUT_1; pc[15:0] = PC_OUT; sys_clk = clk_in; sys_rst = SYS_RESET

  // Notes on the sheet:
  //   HI_LO_WR: pull=down
  //   SP Should be initialized to FFFF
endmodule

module MEMIO (
  input  [5:0] OPCODE_IN,
  input  [9:0] INSTR_DATA_IN,
  input  SYS_CLK_IN,
  input  [15:0] RAM_DATA_IN,
  input  [15:0] REGISTER_X_READ,
  input  [15:0] REGISTER_1_X_READ,
  output [5:0] OPCODE_OUT,
  output [9:0] INSTR_DATA_IN_2,
  output RAM_R_W,
  output [15:0] RAM_ADDR,
  output [15:0] RAM_DATA_OUT,
  output [15:0] REGISTER_X_TO_WRITE,
  output [4:0] REGISTER_READ_ADDRESS,
  output [4:0] REGISTER_WRITE_ADDRESS,
  output [4:0] REGISTER_1_READ_ADDRESS
);

  wire buffer_1_out, comparator_1_lt, LA, LW, LWI, SW, xor_1_out;
  wire [4:0] arg1, arg2, controlled_buffer_1_out;
  wire [5:0] demultiplexer_1_out0, MEM_OPCODE;
  wire [9:0] demultiplexer_2_out0;

  Comparator #(.width(6), .mode("unsigned")) comparator_1 (
    .a(OPCODE_IN), .b(6'b100000), .lt(comparator_1_lt));  // open: gt, eq
  xor xor_1 (xor_1_out, LWI, LW);
  assign controlled_buffer_1_out = xor_1_out ? arg1 : 5'bz;  // Controlled_Buffer controlled_buffer_1
  assign REGISTER_READ_ADDRESS = LW ? arg2 : 5'bz;  // Controlled_Buffer controlled_buffer_2
  assign RAM_ADDR = LW ? REGISTER_X_READ : 16'bz;  // Controlled_Buffer controlled_buffer_3
  assign REGISTER_X_TO_WRITE = LW ? RAM_DATA_IN : 16'bz;  // Controlled_Buffer controlled_buffer_4
  assign REGISTER_READ_ADDRESS = SW ? arg1 : 5'bz;  // Controlled_Buffer controlled_buffer_5
  assign REGISTER_1_READ_ADDRESS = SW ? arg2 : 5'bz;  // Controlled_Buffer controlled_buffer_6
  assign RAM_DATA_OUT = SW ? REGISTER_X_READ : 16'bz;  // Controlled_Buffer controlled_buffer_7
  assign RAM_ADDR = SW ? REGISTER_1_X_READ : 16'bz;  // Controlled_Buffer controlled_buffer_8
  buf buffer_1 (buffer_1_out, comparator_1_lt);
  Comparator #(.width(6), .mode("unsigned")) comparator_2 (.a(MEM_OPCODE), .b(6'b011010), .eq(LA));  // open: gt, lt
  Comparator #(.width(6), .mode("unsigned")) comparator_3 (.a(MEM_OPCODE), .b(6'b011011), .eq(LW));  // open: gt, lt
  Comparator #(.width(6), .mode("unsigned")) comparator_4 (.a(MEM_OPCODE), .b(6'b011100), .eq(SW));  // open: gt, lt
  Comparator #(.width(6), .mode("unsigned")) comparator_5 (.a(MEM_OPCODE), .b(6'b011101), .eq(LWI));  // open: gt, lt
  buf buffer_2 (RAM_R_W, SW);
  Demultiplexer #(.width(6), .disabled(0), .enable("false")) demultiplexer_1 (
    .out0(demultiplexer_1_out0), .out1(MEM_OPCODE), .in(OPCODE_IN), .sel(buffer_1_out));
  Pull_Resistor pull_resistor_1 (.node(buffer_1_out));
  Demultiplexer #(.width(10), .disabled(0), .enable("false")) demultiplexer_2 (
    .out0(demultiplexer_2_out0), .out1({arg1, arg2}), .in(INSTR_DATA_IN), .sel(buffer_1_out));
  assign REGISTER_WRITE_ADDRESS = controlled_buffer_1_out;  // OR_Gate or_1, 5 bits wide OR_Gate
  assign OPCODE_OUT = demultiplexer_1_out0;  // Buffer buffer_3, 6 bits wide
  assign INSTR_DATA_IN_2 = demultiplexer_2_out0;  // Buffer buffer_4, 10 bits wide
  Pull_Resistor pull_resistor_2 (.node(RAM_R_W));
  Pull_Resistor pull_resistor_3 (.node(RAM_ADDR));
  Pull_Resistor pull_resistor_4 (.node(RAM_DATA_OUT));
  Pull_Resistor pull_resistor_5 (.node(REGISTER_X_TO_WRITE));
  Pull_Resistor pull_resistor_6 (.node(REGISTER_READ_ADDRESS));
  Pull_Resistor pull_resistor_7 (.node(REGISTER_WRITE_ADDRESS));
  Pull_Resistor pull_resistor_8 (.node(REGISTER_1_READ_ADDRESS));

  // Other names for the same wires on the sheet: MEM_INSTRUCTION[9:0] = {arg1, arg2}; clk = SYS_CLK_IN;
  //   MEM_ADDRESS[15:0] = RAM_ADDR; MEM_R_W = RAM_R_W; MEMDATA_IN[15:0] = RAM_DATA_IN;
  //   MEMDATA_OUT[15:0] = RAM_DATA_OUT; REGISTER_1_DATA_IN[15:0] = REGISTER_1_X_READ;
  //   REGISTER_DATA_IN[15:0] = REGISTER_X_READ; REGISTER_DATA_OUT[15:0] = REGISTER_X_TO_WRITE
endmodule
